# Fritzing sketch Carbot Schematics (saved by Fritzing 0.9.3b)
breadboards: 2

parts:
  Part1 = Arduino Uno (Rev3)
  R1 = Rotary Potentiometer (Small) [maximum_resistance=100kΩ package=THT]
  M1 = DC Motor
  M2 = DC Motor
  M3 = DC Motor
  M4 = DC Motor
  hc-sr1 = hc-sr04
  hc-sr2 = hc-sr04
  VCC1 = Battery block 9V
  VCC2 = Battery block 9V
  R2 = Resistor [tolerance=±5% resistance=1.1M package="0402 [SMD]"]
  S1 = H-Bridge with L298N
  JACK1 = 2.1mm Barrel Jack with Terminal Block
  U1 = LCD-16X2 [package=lcd-16x2]
  S2 = Pushbutton [package="[THT]"]
  S3 = Pushbutton [package="[THT]"]
  S4 = Pushbutton [package="[THT]"]
  S5 = Pushbutton [package="[THT]"]
  R3 = Resistor [tolerance=±5% resistance=1.1M package="2512 [SMD]"]
  R4 = Resistor [tolerance=±5% resistance=330 package="2010 [SMD]"]
  R5 = Resistor [tolerance=±5% resistance=1.1M package="2512 [SMD]"]
  R6 = Resistor [tolerance=±5% resistance=1.1M package="2512 [SMD]"]
  R7 = Resistor [tolerance=±5% resistance=120k package="2512 [SMD]"]

nets:
  N1: Part1.A2, R2.Pin_0, R4.Pin_1, R5.Pin_1, R6.Pin_1, R7.Pin_1
  N2: Part1.A3, R1.wiper
  N3: Part1.A4/SDA, U1.DB7
  N4: Part1.A5/SCL, U1.DB6
  N5: Part1.D8, hc-sr2.Echo
  N6: Part1.D9_PWM, hc-sr2.Trig
  N7: Part1.D10_PWM/SS, S1.ENB
  N8: Part1.D11_PWM/MOSI, S1.ENA
  GND: Part1.GND, R1.leg2, hc-sr1.GND, hc-sr2.GND, R2.Pin_1, U1.K
  N9: Part1.D2, S1.IN4
  N10: Part1.D3_PWM, S1.IN3
  N11: Part1.D4, S1.IN2
  N12: Part1.D5_PWM, S1.IN1
  N13: Part1.D6_PWM, hc-sr1.Echo
  N14: Part1.D7, hc-sr1.Trig
  VCC: Part1.5V, R1.leg1, hc-sr1.VCC, hc-sr2.VCC, U1.A, S2.Pin_3, S2.Pin_4, S3.Pin_3, S3.Pin_4, S4.Pin_3, S4.Pin_4, S5.Pin_3, S5.Pin_4
  N15: M1.pin_1, M2.pin_2, S1.M1-02
  N16: M1.pin_2, M2.pin_1, S1.M1-01
  N17: M3.pin_1, M4.pin_2, S1.M2-02
  N18: M3.pin_2, M4.pin_1, S1.M2-01
  N19: VCC1.-, JACK1.NEG
  N20: VCC1.+, JACK1.POS
  N21: VCC2.-, S1.GND
  N22: VCC2.+, S1.12V
  N23: S2.Pin_1, S2.Pin_2, R3.Pin_0
  N24: S3.Pin_1, S3.Pin_2, R6.Pin_0
  N25: S4.Pin_1, R4.Pin_0
  N26: S5.Pin_1, R7.Pin_0
  N27: R3.Pin_1, R5.Pin_0

notes:
  GND (LCD)
  VCC (LCD)
  SDA (LCD)
  SCL (LCD)

custom parts:
  H-Bridge with L298N: h-bridge
